// Logisim project AddCalc.circ as structural Verilog
module AddCalc (
  input  [31:0] _32b,
  input  [31:0] _32b_2,
  output [15:0] \EndereçoDeDados 
);

  wire [4:0] bitfinder_1_index;
  wire [31:0] adder_1_out;

  Adder #(.width(32)) adder_1 (.a(_32b), .b(_32b_2), .out(adder_1_out));  // open: cin, cout
  BitFinder #(.width(32)) bitfinder_1 (.in(adder_1_out), .index(bitfinder_1_index));  // open: found
endmodule
