// Logisim project BancoDeRegistradores.circ as structural Verilog: 1 circuit, main circuit main
module main (
);

  wire decoder_1_out0, decoder_1_out1, decoder_1_out2, decoder_1_out3, decoder_1_out4, decoder_1_out5,
       decoder_1_out6, decoder_1_out7, decoder_1_out8, decoder_1_out9, decoder_1_out10, decoder_1_out11,
       decoder_1_out12, decoder_1_out13, decoder_1_out14, decoder_1_out15, decoder_1_out16, decoder_1_out17,
       decoder_1_out18, decoder_1_out19, decoder_1_out20, decoder_1_out21, decoder_1_out22, decoder_1_out23,
       decoder_1_out24, decoder_1_out25, decoder_1_out26, decoder_1_out27, decoder_1_out28, decoder_1_out29,
       decoder_1_out30, decoder_1_out31;
  wire [31:0] register_1_q, register_2_q, register_3_q, register_4_q, register_5_q, register_6_q,
       register_7_q, register_8_q, register_9_q, register_10_q, register_11_q, register_12_q, register_13_q,
       register_14_q, register_15_q, register_16_q, register_17_q, register_18_q, register_19_q,
       register_27_q;

  Decoder #(.select(5)) decoder_1 (
    .out0(decoder_1_out0), .out1(decoder_1_out1), .out2(decoder_1_out2), .out3(decoder_1_out3),
    .out4(decoder_1_out4), .out5(decoder_1_out5), .out6(decoder_1_out6), .out7(decoder_1_out7),
    .out8(decoder_1_out8), .out9(decoder_1_out9), .out10(decoder_1_out10), .out11(decoder_1_out11),
    .out12(decoder_1_out12), .out13(decoder_1_out13), .out14(decoder_1_out14), .out15(decoder_1_out15),
    .out16(decoder_1_out16), .out17(decoder_1_out17), .out18(decoder_1_out18), .out19(decoder_1_out19),
    .out20(decoder_1_out20), .out21(decoder_1_out21), .out22(decoder_1_out22), .out23(decoder_1_out23),
    .out24(decoder_1_out24), .out25(decoder_1_out25), .out26(decoder_1_out26), .out27(decoder_1_out27),
    .out28(decoder_1_out28), .out29(decoder_1_out29), .out30(decoder_1_out30), .out31(decoder_1_out31));  // open: sel, en
  Register #(.width(32)) register_1 (.en(decoder_1_out0), .Q(register_1_q));  // open: D, clk, clr
  Register #(.width(32)) register_2 (.en(decoder_1_out1), .Q(register_2_q));  // open: D, clk, clr
  Register #(.width(32)) register_3 (.en(decoder_1_out2), .Q(register_3_q));  // open: D, clk, clr
  Register #(.width(32)) register_4 (.en(decoder_1_out3), .Q(register_4_q));  // open: D, clk, clr
  Register #(.width(32)) register_5 (.en(decoder_1_out4), .Q(register_5_q));  // open: D, clk, clr
  Register #(.width(32)) register_6 (.en(decoder_1_out5), .Q(register_6_q));  // open: D, clk, clr
  Register #(.width(32)) register_7 (.en(decoder_1_out6), .Q(register_7_q));  // open: D, clk, clr
  Register #(.width(32)) register_8 (.en(decoder_1_out7), .Q(register_8_q));  // open: D, clk, clr
  Register #(.width(32)) register_9 (.en(decoder_1_out8), .Q(register_9_q));  // open: D, clk, clr
  Register #(.width(32)) register_10 (.en(decoder_1_out9), .Q(register_10_q));  // open: D, clk, clr
  Register #(.width(32)) register_11 (.en(decoder_1_out10), .Q(register_11_q));  // open: D, clk, clr
  Register #(.width(32)) register_12 (.en(decoder_1_out11), .Q(register_12_q));  // open: D, clk, clr
  Register #(.width(32)) register_13 (.en(decoder_1_out12), .Q(register_13_q));  // open: D, clk, clr
  Register #(.width(32)) register_14 (.en(decoder_1_out14), .Q(register_14_q));  // open: D, clk, clr
  Register #(.width(32)) register_15 (.en(decoder_1_out13), .Q(register_15_q));  // open: D, clk, clr
  Register #(.width(32)) register_16 (.en(decoder_1_out15), .Q(register_16_q));  // open: D, clk, clr
  Register #(.width(32)) register_17 (.en(decoder_1_out16), .Q(register_17_q));  // open: D, clk, clr
  Register #(.width(32)) register_18 (.Q(register_18_q));  // open: D, en, clk, clr
  Register #(.width(32)) register_19 (.Q(register_19_q));  // open: D, en, clk, clr
  Register #(.width(32)) register_20 ();  // open: D, en, Q, clk, clr
  Register #(.width(32)) register_21 ();  // open: D, en, Q, clk, clr
  Register #(.width(32)) register_22 ();  // open: D, en, Q, clk, clr
  Register #(.width(32)) register_23 ();  // open: D, en, Q, clk, clr
  Register #(.width(32)) register_24 ();  // open: D, en, Q, clk, clr
  Register #(.width(32)) register_25 ();  // open: D, en, Q, clk, clr
  Register #(.width(32)) register_26 ();  // open: D, en, Q, clk, clr
  Register #(.width(32)) register_27 (.Q(register_27_q));  // open: D, en, clk, clr
  Register #(.width(32)) register_28 ();  // open: D, en, Q, clk, clr
  Register #(.width(32)) register_29 ();  // open: D, en, Q, clk, clr
  Register #(.width(32)) register_30 ();  // open: D, en, Q, clk, clr
  Register #(.width(32)) register_31 ();  // open: D, en, Q, clk, clr
  Register #(.width(32)) register_32 ();  // open: D, en, Q, clk, clr
  Multiplexer #(.select(5), .width(32)) multiplexer_1 (
    .in0(register_1_q), .in1(register_2_q), .in2(register_3_q), .in3(register_4_q), .in4(register_5_q),
    .in5(register_6_q), .in6(register_7_q), .in7(register_8_q), .in8(register_9_q), .in9(register_10_q),
    .in10(register_11_q), .in11(register_12_q), .in12(register_13_q), .in13(register_14_q),
    .in14(register_15_q), .in15(register_16_q), .in16(register_17_q), .in17(register_27_q),
    .in18(register_18_q), .in19(register_19_q));  // open: in20, in21, in22, in23, in24, in25, in26, in27, in28, in29, in30, in31, out, sel, en
  Multiplexer #(.select(5), .width(32)) multiplexer_2 (
    .in0(register_1_q), .in1(register_2_q), .in2(register_3_q), .in3(register_4_q), .in4(register_5_q),
    .in5(register_6_q), .in6(register_7_q), .in7(register_8_q), .in8(register_9_q), .in9(register_10_q),
    .in10(register_11_q), .in11(register_12_q), .in12(register_13_q), .in13(register_14_q),
    .in14(register_15_q), .in15(register_16_q), .in16(register_17_q), .in17(register_27_q),
    .in18(register_18_q), .in19(register_19_q));  // open: in20, in21, in22, in23, in24, in25, in26, in27, in28, in29, in30, in31, out, sel, en
endmodule
