// Logisim project CircuitoVD.circ as structural Verilog: 1 circuit, main circuit main
module main (
  input  [31:0] in_1,
  input  [31:0] in_2,
  input  [31:0] in_3,
  input  [31:0] in_4,
  input  [1:0] in_5,
  output [31:0] out_6
);

  wire [31:0] adder_1_out, shifter_1_out;

  Adder #(.width(32)) adder_1 (.a(32'h8), .b(in_1), .out(adder_1_out));  // open: cin, cout
  Shifter #(.width(32)) shifter_1 (.in(in_2), .\dist (5'b10000), .out(shifter_1_out));
  Multiplexer #(.select(2), .width(32)) multiplexer_1 (
    .in0(adder_1_out), .in1(shifter_1_out), .in2(in_3), .in3(in_4), .out(out_6), .sel(in_5));  // open: en
endmodule
