// Logisim project NextPC.circ as structural Verilog: 1 circuit, main circuit main
module main (
  input  [31:0] IMMD16,
  input  [31:0] PC,
  input  [31:0] IMMD26,
  input  [31:0] VS,
  input  [1:0] PC_SEL,
  output [31:0] nextPC
);

  wire [31:0] adder_1_out, adder_2_out, adder_3_out, and_1_out, shifter_1_out, shifter_2_out;

  Shifter #(.width(32)) shifter_1 (.in(IMMD16), .\dist (5'b00010), .out(shifter_1_out));
  assign and_1_out = PC & 32'hf0000000;  // AND_Gate and_1, 32 bits wide
  Shifter #(.width(32)) shifter_2 (.in(IMMD26), .\dist (5'b00010), .out(shifter_2_out));
  Adder #(.width(32)) adder_1 (.a(shifter_1_out), .b(PC), .out(adder_1_out));  // open: cin, cout
  Adder #(.width(32)) adder_2 (.a(32'h4), .b(PC), .out(adder_2_out));  // open: cin, cout
  Adder #(.width(32)) adder_3 (.a(and_1_out), .b(shifter_2_out), .out(adder_3_out));  // open: cin, cout
  Multiplexer #(.select(2), .width(32)) multiplexer_1 (
    .in0(adder_1_out), .in1(adder_2_out), .in2(adder_3_out), .in3(VS), .out(nextPC), .sel(PC_SEL));  // open: en
endmodule
