// Logisim project ULASegundoOperando.circ as structural Verilog
module ULASegundo (
  input  [31:0] IMMD16,
  input  [31:0] VB,
  input  [4:0] SHAMT,
  input  [1:0] ULA_Operando_sel,
  output [31:0] OPERANDO
);

  wire [31:0] bit_extender_1_out;

  assign bit_extender_1_out = {{27{1'b0}}, SHAMT};  // Bit_Extender bit_extender_1
  Multiplexer #(.select(2), .width(32)) multiplexer_1 (
    .in0(IMMD16), .in1(VB), .in2(bit_extender_1_out), .out(OPERANDO), .sel(ULA_Operando_sel));  // open: in3, en
endmodule
