// Logisim project separador.circ as structural Verilog: 1 circuit, main circuit main
module main (
  input  [31:0] in_1,
  output [31:0] IMMD26,
  output [31:0] IMMD16,
  output [5:0] FUNCT,
  output [4:0] SHAMT,
  output [4:0] RD,
  output [4:0] RT,
  output [4:0] RS,
  output [5:0] opcode
);

  assign IMMD26 = {{6{1'b0}}, in_1[25:0]};  // Bit_Extender bit_extender_1
  assign IMMD16 = {{16{1'b0}}, in_1[15:0]};  // Bit_Extender bit_extender_2

  assign FUNCT = in_1[5:0];
  assign opcode = in_1[31:26];
  assign RD = in_1[15:11];
  assign RS = in_1[25:21];
  assign RT = in_1[20:16];
  assign SHAMT = in_1[10:6];
endmodule
